# Fritzing sketch Avionica (saved by Fritzing 0.9.10b)
perfboards: 1

parts:
  M1 = BME680 Module [part_number=CJMCU-680]  # not connected
  Part1 = Adafruit LSM9DS1 9DoF Breakout [part_number="Adafruit #3387"]
  microSD1 = MicroSD Card Module
  ZS-042_RTC1 = ZS-042 RTC Module
  HTCC-AB02S1 = Heltec HTCC-AB02S GPS Dev Board

nets:
  N1: Part1.CS_AG, HTCC-AB02S1.GPIO13
  GND: microSD1.GND, ZS-042_RTC1.GND, HTCC-AB02S1.GND1
  VCC: microSD1.VCC, ZS-042_RTC1.VCC, HTCC-AB02S1.VDD, HTCC-AB02S1.GPIO7
  N2: microSD1.MISO, HTCC-AB02S1.MISO
  N3: microSD1.MOSI, HTCC-AB02S1.MOSI
  N4: microSD1.SCK, HTCC-AB02S1.CLK
  N5: microSD1.CS, HTCC-AB02S1.GPIO11
  N6: ZS-042_RTC1.SDA, HTCC-AB02S1.SDA
  N7: ZS-042_RTC1.SCL, HTCC-AB02S1.SCL

custom parts:
  BME680 Module: Bosch BME680 Development Module The BME680 is a digital 4-in-1 sensor that measures air quality [gas], humidity, pressure and temperature. Links: BME680 product datasheet
  Adafruit LSM9DS1 9DoF Breakout: Add motion, direction and orientation sensing to your Arduino project with this all-in-one 9-DOF sensor. Inside the chip are three sensors, one is a classic 3-axis accelerometer, which can tell you which direction is down towards the Earth (by measuring gravity) or how fast the board is accelerating in 3D space. The other is a 3-axis magnetometer that can sense where the strongest magnetic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
